# Fritzing sketch Arduino-prototype (saved by Fritzing 0.9.2b)
breadboards: 1

parts:
  Part1 = Arduino Uno (Rev3)
  LED1 = 7-SEGMENT-4DIGIT-YOUNGSUN [package=7-segment-4digit-youngsun]

nets:
  N1: Part1.A0, LED1.E
  N2: Part1.A1, LED1.A
  N3: Part1.D8, LED1.G
  N4: Part1.D9_PWM, LED1.DIG3
  N5: Part1.D10_PWM/SS, LED1.DIG2
  N6: Part1.D11_PWM/MOSI, LED1.DIG1, LED1.COL-A
  N7: Part1.D12/MISO, LED1.COL-C
  N8: Part1.D3_PWM, LED1.B
  N9: Part1.D4, LED1.C
  N10: Part1.D5_PWM, LED1.D
  N11: Part1.D6_PWM, LED1.DIG4
  N12: Part1.D7, LED1.F
